// Digital circuit 8BitProzessor MitRam.dig as structural Verilog
module _8BitProzessor_MitRam (
  input  [23:0] DataBus_in,
  input  RDY,
  input  Clock_M,
  input  Clock_A,
  output [23:0] DataBus_out,
  output [23:0] AddBus,
  output WR,
  output RD,
  output [7:0] IterationPoint,
  output [23:0] A,
  output [23:0] B,
  output [23:0] Y,
  output [23:0] R_1,
  output [23:0] IP,
  output [23:0] IR,
  output [23:0] MAR,
  output [23:0] MDR,
  output [23:0] R_2,
  output [23:0] R_3,
  output [23:0] R_0,
  output [23:0] Akk
);

  wire ALU__0, ALU_ca, ALU_out_7, controlunit_1_a_in, controlunit_1_alu_out, controlunit_1_b_in,
       controlunit_1_ip_in, controlunit_1_ip_out, controlunit_1_ir_in, controlunit_1_ir_op_out,
       controlunit_1_mar_in, controlunit_1_mdr_in, controlunit_1_mdr_out, controlunit_1_r_in,
       controlunit_1_r_out, controlunit_1_y_in, controlunit_1_y_out, or_2_out;
  wire [1:0] controlunit_1_sr_eq_ropx;
  wire [3:0] controlunit_1_f_eq_x;
  wire [23:0] ALU_o, demultiplexer_1_out_0, demultiplexer_1_out_1, demultiplexer_1_out_2,
       demultiplexer_1_out_3, driver_1_out, multiplexer_1_out, or_1_out;

  assign driver_1_out = controlunit_1_mdr_out ? DataBus_out : 24'bz;  // Driver driver_1
  assign driver_1_out = controlunit_1_ir_op_out ? IR : 24'bz;  // Driver driver_2
  assign driver_1_out = controlunit_1_ip_out ? IP : 24'bz;  // Driver driver_3
  assign driver_1_out = controlunit_1_r_out ? multiplexer_1_out : 24'bz;  // Driver driver_4
  assign driver_1_out = controlunit_1_y_out ? Y : 24'bz;  // Driver driver_5
  assign driver_1_out = controlunit_1_alu_out ? Akk : 24'bz;  // Driver driver_6
  Demultiplexer #(.Selector_Bits(2), .Bits(24)) demultiplexer_1 (
    .sel(controlunit_1_sr_eq_ropx), .in(driver_1_out), .out_0(demultiplexer_1_out_0),
    .out_1(demultiplexer_1_out_1), .out_2(demultiplexer_1_out_2), .out_3(demultiplexer_1_out_3));
  assign or_1_out = DataBus_in | driver_1_out;  // Or or_1, 24 bits wide
  _24_BitRegister u_MDR (.I(or_1_out), .W(controlunit_1_mdr_in), .R(1'b1), .O(DataBus_out));
  _24_BitRegister u_MAR (.I(driver_1_out), .W(controlunit_1_mar_in), .R(1'b1), .O(AddBus));
  _24_BitRegister IR_InstructionRegister (.I(driver_1_out), .W(controlunit_1_ir_in), .R(1'b1), .O(IR));
  _24_BitRegister IP_InstructionPointer (.I(driver_1_out), .W(controlunit_1_ip_in), .R(1'b1), .O(IP));
  _24_BitRegister u_Y (.I(driver_1_out), .W(controlunit_1_y_in), .R(1'b1), .O(Y));
  _24_BitRegister _24_bitregister_1 (.I(ALU_o), .W(controlunit_1_a_in), .R(1'b1), .O(Akk));
  _24_BitRegister u_A (.I(driver_1_out), .W(controlunit_1_a_in), .R(1'b1), .O(A));
  _24BitALU ALU (.A(A), .B(B), .S(controlunit_1_f_eq_x), .O(ALU_o), .Ca(ALU_ca), ._0(ALU__0), .out_7(ALU_out_7));
  _24_BitRegister u_R_0 (.I(demultiplexer_1_out_0), .W(controlunit_1_r_in), .R(1'b1), .O(R_3));
  _24_BitRegister u_R_1 (.I(demultiplexer_1_out_1), .W(controlunit_1_r_in), .R(1'b1), .O(R_2));
  _24_BitRegister u_R_2 (.I(demultiplexer_1_out_2), .W(controlunit_1_r_in), .R(1'b1), .O(R_1));
  _24_BitRegister u_R_3 (.I(demultiplexer_1_out_3), .W(controlunit_1_r_in), .R(1'b1), .O(R_0));
  _24_BitRegister u_B (.I(driver_1_out), .W(controlunit_1_b_in), .R(1'b1), .O(B));
  RAMDualPort ramdualport_1 ();  // open: A, Din, str, C, ld, D
  BlockRAMDualPort blockramdualport_1 ();  // open: A, Din, str, C, D
  Multiplexer #(.Selector_Bits(2), .Bits(24)) multiplexer_1 (
    .sel(controlunit_1_sr_eq_ropx), .in_0(R_3), .in_1(R_2), .in_2(R_1), .in_3(R_0), .out(multiplexer_1_out));
  RAMSinglePort ramsingleport_1 ();  // open: A, str, C, ld, D
  RAMSinglePortSel ramsingleportsel_1 ();  // open: A, CS, WE, OE, D
  RegisterFile registerfile_1 ();  // open: Din, we, Rw, C, Ra, Rb, Da, Db
  ControlUnit controlunit_1 (
    .MDR_in(controlunit_1_mdr_in), .MDR_out(controlunit_1_mdr_out), .MAR_in(controlunit_1_mar_in),
    .Decodierung(IR), .IR_in(controlunit_1_ir_in), .IR_op_out(controlunit_1_ir_op_out),
    .IP_in(controlunit_1_ip_in), .IP_out(controlunit_1_ip_out), .R_in(controlunit_1_r_in),
    .R_out(controlunit_1_r_out), .SR_eq_ROPx(controlunit_1_sr_eq_ropx), .Y_in(controlunit_1_y_in),
    .Y_out(controlunit_1_y_out), .B_in(controlunit_1_b_in), .A_in(controlunit_1_a_in),
    .ALU_out(controlunit_1_alu_out), .F_eq_x(controlunit_1_f_eq_x), .Ca(ALU_ca), ._0(ALU__0),
    .in_21(ALU_out_7), .WR(WR), .RD(RD), .RDY(1'b1), .clock(or_2_out), .IterationPoint(IterationPoint));
  RAMDualAccess ramdualaccess_1 ();  // open: str, C, ld, A1, Din1, A2, D1, D2
  RAMAsync ramasync_1 ();  // open: A, D, we, Q
  or or_2 (or_2_out, Clock_M, Clock_A);

  assign MAR = AddBus;
  assign MDR = DataBus_out;

  // Notes on the sheet:
  //   CPU
endmodule
