// Digital circuit 8BitProzessorVisualization.dig as structural Verilog
module _8BitProzessorVisualization (
  input  [23:0] DataBus_in,
  input  RDY,
  input  Clock_M,
  input  Clock_A,
  input  Enable,
  output [23:0] DataBus_out,
  output [23:0] AddBus,
  output WR,
  output RD,
  output [7:0] IterationPoint,
  output [23:0] A,
  output [23:0] B,
  output [23:0] Y,
  output [23:0] R_1,
  output [23:0] IP,
  output [7:0] IR,
  output [23:0] MAR,
  output [7:0] MDR_OP,
  output [23:0] R_2,
  output [23:0] R_3,
  output [23:0] R_0,
  output [23:0] Akk,
  output [23:0] Bus,
  output [7:0] MDR_A1,
  output [7:0] MDR_A0,
  output [23:0] MDR
);

  wire _8bitin1bit_1_out, _24bitin1bit_1_out, ALU__0, ALU_ca, ALU_out_7, and_1_out, controlunit_1_p1,
       controlunit_1_p2, controlunit_1_p3, controlunit_1_p4, controlunit_1_p5, controlunit_1_p6,
       controlunit_1_p7, controlunit_1_p9, controlunit_1_p10, controlunit_1_p11, controlunit_1_p12,
       controlunit_1_p13, controlunit_1_p14, controlunit_1_p16, controlunit_1_p17, controlunit_1_p18,
       controlunit_1_p19, controlunit_1_p20, controlunit_1_p25, controlunit_1_p29, not_1_out, or_2_out;
  wire [1:0] controlunit_1_p15;
  wire [3:0] controlunit_1_p21, delay_1_out;
  wire [7:0] or_1_out, or_1_out_2, or_1_out_3;
  wire [23:0] ALU_o, demultiplexer_1_out_0, demultiplexer_1_out_1, demultiplexer_1_out_2,
       demultiplexer_1_out_3, multiplexer_1_out, multiplexer_2_out, pulldown_1_out, ramasync_1_q;
  wire [23:8] IR_t, MDR_A0_t, MDR_A1_t, MDR_OP_t;

  assign Bus = controlunit_1_p3 ? DataBus_out : 24'bz;  // Driver driver_1
  assign Bus = controlunit_1_p4 ? {MDR_A0_t, MDR_A0} : 24'bz;  // Driver driver_2
  assign Bus = controlunit_1_p5 ? {MDR_A1_t, MDR_A1} : 24'bz;  // Driver driver_3
  assign Bus = controlunit_1_p6 ? {MDR_OP_t, MDR_OP} : 24'bz;  // Driver driver_4
  assign Bus = controlunit_1_p10 ? {IR_t, IR} : 24'bz;  // Driver driver_5
  assign Bus = controlunit_1_p12 ? IP : 24'bz;  // Driver driver_6
  assign Bus = controlunit_1_p14 ? multiplexer_2_out : 24'bz;  // Driver driver_7
  assign Bus = controlunit_1_p17 ? Y : 24'bz;  // Driver driver_8
  assign Bus = controlunit_1_p20 ? Akk : 24'bz;  // Driver driver_9
  Demultiplexer #(.Selector_Bits(2), .Bits(24)) demultiplexer_1 (
    .sel(controlunit_1_p15), .in(Bus), .out_0(demultiplexer_1_out_0), .out_1(demultiplexer_1_out_1),
    .out_2(demultiplexer_1_out_2), .out_3(demultiplexer_1_out_3));
  assign {or_1_out_3, or_1_out_2, or_1_out} = pulldown_1_out | DataBus_in;  // Or or_1, 24 bits wide
  Multiplexer #(.Bits(24)) multiplexer_1 (
    .sel(controlunit_1_p1), .in_0({or_1_out_3, or_1_out_2, or_1_out}), .in_1(Bus), .out(multiplexer_1_out));
  _24_BitRegister u_MDR (.I(multiplexer_1_out), .W(or_2_out), .R(1'b1), .O(DataBus_out));
  _24_BitRegister u_MDR_A0 (.I({{16{1'b0}}, or_1_out}), .W(controlunit_1_p2), .R(1'b1), .O({MDR_A0_t, MDR_A0}));
  _24_BitRegister u_MDR_A1 (.I({{16{1'b0}}, or_1_out_2}), .W(controlunit_1_p2), .R(1'b1), .O({MDR_A1_t, MDR_A1}));
  _24_BitRegister u_MDR_OP (.I({{16{1'b0}}, or_1_out_3}), .W(controlunit_1_p2), .R(1'b1), .O({MDR_OP_t, MDR_OP}));
  _24_BitRegister u_MAR (.I(Bus), .W(controlunit_1_p7), .R(1'b1), .O(AddBus));
  _24_BitRegister IR_InstructionRegister (.I(Bus), .W(controlunit_1_p9), .R(1'b1), .O({IR_t, IR}));
  _24_BitRegister IP_InstructionPointer (.I(Bus), .W(controlunit_1_p11), .R(1'b1), .O(IP));
  _24_BitRegister u_Y (.I(Bus), .W(controlunit_1_p16), .R(1'b1), .O(Y));
  Delay #(.Bits(4), .delayTime(2)) delay_1 (.in(controlunit_1_p21), .out(delay_1_out));
  _24_BitRegister Akkumulator (.I(ALU_o), .W(_8bitin1bit_1_out), .R(1'b1), .O(Akk));
  _24_BitRegister u_A (.I(Bus), .W(controlunit_1_p19), .R(1'b1), .O(A));
  _24BitALU ALU (.A(A), .B(B), .S(delay_1_out), .O(ALU_o), .Ca(ALU_ca), ._0(ALU__0), .out_7(ALU_out_7));
  _8BitIn1Bit _8bitin1bit_1 (.in({4'b0000, controlunit_1_p21}), .out(_8bitin1bit_1_out));
  _24_BitRegister u_R_0 (.I(demultiplexer_1_out_0), .W(controlunit_1_p13), .R(1'b1), .O(R_0));
  _24_BitRegister u_R_1 (.I(demultiplexer_1_out_1), .W(controlunit_1_p13), .R(1'b1), .O(R_1));
  _24_BitRegister u_R_2 (.I(demultiplexer_1_out_2), .W(controlunit_1_p13), .R(1'b1), .O(R_2));
  _24_BitRegister u_R_3 (.I(demultiplexer_1_out_3), .W(controlunit_1_p13), .R(1'b1), .O(R_3));
  _24_BitRegister u_B (.I(Bus), .W(controlunit_1_p18), .R(1'b1), .O(B));
  RAMAsync #(.AddrBits(8), .Bits(24)) ramasync_1 (.A(AddBus[7:0]), .D(DataBus_out), .we(WR), .Q(ramasync_1_q));
  or or_2 (or_2_out, RD, controlunit_1_p1);
  Multiplexer #(.Selector_Bits(2), .Bits(24)) multiplexer_2 (
    .sel(controlunit_1_p15), .in_0(R_0), .in_1(R_1), .in_2(R_2), .in_3(R_3), .out(multiplexer_2_out));
  PullDown #(.Bits(24)) pulldown_1 (.out(pulldown_1_out));
  assign pulldown_1_out = RD ? ramasync_1_q : 24'bz;  // Driver driver_10
  _24BitIn1Bit _24bitin1bit_1 (.in(pulldown_1_out), .out(_24bitin1bit_1_out));
  not not_1 (not_1_out, _24bitin1bit_1_out);
  // ControlUnit controlunit_1: pin names not known; wires that end beside it: controlunit_1_p1, controlunit_1_p2, controlunit_1_p3, controlunit_1_p4, controlunit_1_p5, controlunit_1_p6, controlunit_1_p7, {IR_t, IR}, controlunit_1_p9, controlunit_1_p10, controlunit_1_p11, controlunit_1_p12, controlunit_1_p13, controlunit_1_p14, controlunit_1_p15, controlunit_1_p16, controlunit_1_p17, controlunit_1_p18, controlunit_1_p19, controlunit_1_p20, controlunit_1_p21, ALU_ca, ALU__0, ALU_out_7, controlunit_1_p25, IterationPoint, WR, RD, controlunit_1_p29
  or or_3 (controlunit_1_p29, RDY, not_1_out);
  and and_1 (and_1_out, Clock_A, Enable);
  or or_4 (controlunit_1_p25, Clock_M, and_1_out);

  assign MAR = AddBus;
  assign MDR = DataBus_out;

  // Other names for the same wires on the sheet: IR_t[7:0] = IR; IterrationPointer[7:0] = IterationPoint;
  //   MDR_A0_t[7:0] = MDR_A0; MDR_A1_t[7:0] = MDR_A1; MDR_OP_t[7:0] = MDR_OP

  // Notes on the sheet:
  //   Clock_A: Hz: 10
  //   24 Bits -> 8Bit OP , 8BitA1, 8BitA0
  //   A means The Address (direct)
  //   Reg means the Value of the Address (Indirect)
  //   00 - 0
  //   03 - ADD Reg0 on Reg1
  //   08 - JumpTo  Reg0 (global)
  //   10 - JumpTo Reg0 if Reg1 is Pos
  //   Stats
  //   RamConnection
  //   CPU
  //   Clock
endmodule
