// Digital circuit ControlUnit.dig as structural Verilog
module ControlUnit (
  input  [23:0] Decodierung,
  input  Ca,
  input  _0,
  input  in_21,
  input  RDY,
  input  clock,
  output MDR_in,
  output MDR_outOP,
  output MAR_in,
  output WR,
  output RD,
  output IR_in,
  output IR_op_out,
  output IP_in,
  output IP_out,
  output R_in,
  output R_out,
  output [1:0] SR_eq_ROPx,
  output B_in,
  output Y_in,
  output Y_out,
  output A_in,
  output ALU_out,
  output [3:0] F_eq_x,
  output [7:0] IterationPoint,
  output MDR_outA0,
  output MDR_outA1
);

  wire _8bitin1bit_1_out, and_1_out, and_2_out, delay_1_out, kombinatorischeschaltung_1_p2,
       kombinatorischeschaltung_1_p3, kombinatorischeschaltung_1_p4, kombinatorischeschaltung_1_p5,
       kombinatorischeschaltung_1_p32, kombinatorischeschaltung_1_p33, multiplexer_2_out, multiplexer_3_out,
       undriven;
  wire [7:0] kombinatorischeschaltung_1_p31, multiplexer_1_out;

  Multiplexer #(.Bits(8)) multiplexer_1 (
    .sel(kombinatorischeschaltung_1_p33), .in_0(kombinatorischeschaltung_1_p31), .in_1(Decodierung[23:16]),
    .out(multiplexer_1_out));
  _8BitIn1Bit _8bitin1bit_1 (.in(Decodierung[23:16]), .out(_8bitin1bit_1_out));
  and and_1 (and_1_out, RDY, clock);
  Multiplexer multiplexer_2 (.sel(delay_1_out), .in_0(clock), .in_1(and_1_out), .out(multiplexer_2_out));
  and and_2 (and_2_out, ~_8bitin1bit_1_out, kombinatorischeschaltung_1_p33);  // And
  // KombinatorischeSchaltung kombinatorischeschaltung_1: pin names not known; wires that end beside it: MDR_in, kombinatorischeschaltung_1_p2, kombinatorischeschaltung_1_p3, kombinatorischeschaltung_1_p4, kombinatorischeschaltung_1_p5, RD, MDR_outA1, MDR_outA0, MDR_outOP, MAR_in, IR_in, IR_op_out, IP_in, IP_out, R_in, R_out, SR_eq_ROPx, Y_in, IterationPoint, Y_out, B_in, A_in, ALU_out, F_eq_x, kombinatorischeschaltung_1_p2, kombinatorischeschaltung_1_p3, kombinatorischeschaltung_1_p4, kombinatorischeschaltung_1_p5, RD, WR, kombinatorischeschaltung_1_p31, kombinatorischeschaltung_1_p32, kombinatorischeschaltung_1_p33
  Multiplexer multiplexer_3 (
    .sel(and_2_out), .in_0(kombinatorischeschaltung_1_p32), .in_1(1'b1), .out(multiplexer_3_out));
  Delay delay_1 (.in(undriven), .out(delay_1_out));
  \_8BitSequenzenzähler  \_8bitsequenzenzähler_1  (
    .C(multiplexer_2_out), .JT(multiplexer_1_out), .R(multiplexer_3_out), .Add(IterationPoint));
endmodule
