// Digital circuit KombinatorischeSchaltung.dig as structural Verilog
module KombinatorischeSchaltung (
  input  [7:0] S_equenz,
  output MDR_in,
  output MDR_out,
  output MAR_in,
  output IR_in,
  output IR_op_out,
  output IP_in,
  output IP_out,
  output R_in,
  output R_out,
  output [1:0] SR_eq_ROPx,
  output B_in,
  output Y_in,
  output Y_out,
  output A_in,
  output ALU_out,
  output [3:0] F_eq_x,
  output WR,
  output RD,
  output RDY,
  output Ca,
  output _0,
  output out_22,
  output [7:0] NA,
  output R,
  output De,
  output WRDY
);

  wire demultiplexer_1_out_0, demultiplexer_1_out_1, demultiplexer_1_out_2, demultiplexer_1_out_3,
       demultiplexer_1_out_4, demultiplexer_1_out_5, demultiplexer_1_out_6, demultiplexer_1_out_7;

  Demultiplexer #(.Selector_Bits(3)) demultiplexer_1 (
    .sel(S_equenz[2:0]), .in(1'b1), .out_0(demultiplexer_1_out_0), .out_1(demultiplexer_1_out_1),
    .out_2(demultiplexer_1_out_2), .out_3(demultiplexer_1_out_3), .out_4(demultiplexer_1_out_4),
    .out_5(demultiplexer_1_out_5), .out_6(demultiplexer_1_out_6), .out_7(demultiplexer_1_out_7));
  PullDown pulldown_1 (.out(MDR_in));
  assign MDR_in = demultiplexer_1_out_0 ? 1'b1 : 1'bz;  // Driver driver_1
  assign MDR_out = demultiplexer_1_out_2 ? 1'b1 : 1'bz;  // Driver driver_2
  PullDown pulldown_2 (.out(MDR_out));
  assign MAR_in = demultiplexer_1_out_0 ? 1'b1 : 1'bz;  // Driver driver_3
  PullDown pulldown_3 (.out(MAR_in));
  assign IR_in = demultiplexer_1_out_2 ? 1'b1 : 1'bz;  // Driver driver_4
  PullDown pulldown_4 (.out(IR_in));
  PullDown pulldown_5 (.out(1'b0));
  assign IP_in = demultiplexer_1_out_1 ? 1'b1 : 1'bz;  // Driver driver_5
  PullDown pulldown_6 (.out(IP_in));
  assign IP_out = demultiplexer_1_out_0 ? 1'b1 : 1'bz;  // Driver driver_6
  PullDown pulldown_7 (.out(IP_out));
  assign R_in = demultiplexer_1_out_5 ? 1'b1 : 1'bz;  // Driver driver_7
  PullDown pulldown_8 (.out(R_in));
  PullDown pulldown_9 (.out(R_out));
  assign R_out = demultiplexer_1_out_3 ? 1'b1 : 1'bz;  // Driver driver_8
  assign R_out = demultiplexer_1_out_4 ? 1'b1 : 1'bz;  // Driver driver_9
  assign SR_eq_ROPx = demultiplexer_1_out_3 ? 2'b01 : 2'bz;  // Driver driver_10
  assign SR_eq_ROPx = demultiplexer_1_out_4 ? 2'b10 : 2'bz;  // Driver driver_11
  assign SR_eq_ROPx = demultiplexer_1_out_5 ? 2'b01 : 2'bz;  // Driver driver_12
  PullDown #(.Bits(2)) pulldown_10 (.out(SR_eq_ROPx));
  PullDown pulldown_11 (.out(1'b0));
  PullDown pulldown_12 (.out(1'b0));
  PullDown pulldown_13 (.out(B_in));
  assign B_in = demultiplexer_1_out_4 ? 1'b1 : 1'bz;  // Driver driver_13
  assign A_in = demultiplexer_1_out_0 ? 1'b1 : 1'bz;  // Driver driver_14
  assign A_in = demultiplexer_1_out_3 ? 1'b1 : 1'bz;  // Driver driver_15
  PullDown pulldown_14 (.out(A_in));
  assign ALU_out = demultiplexer_1_out_1 ? 1'b1 : 1'bz;  // Driver driver_16
  assign ALU_out = demultiplexer_1_out_5 ? 1'b1 : 1'bz;  // Driver driver_17
  PullDown pulldown_15 (.out(ALU_out));
  assign F_eq_x = demultiplexer_1_out_0 ? 4'b0110 : 4'bz;  // Driver driver_18
  assign F_eq_x = demultiplexer_1_out_4 ? 4'b0001 : 4'bz;  // Driver driver_19
  PullDown #(.Bits(4)) pulldown_16 (.out(F_eq_x));
  PullDown pulldown_17 (.out(1'b0));
  PullDown pulldown_18 (.out(1'b0));
  PullDown pulldown_19 (.out(1'b0));
  PullDown pulldown_20 (.out(1'b0));
  PullDown pulldown_21 (.out(RD));
  assign RD = demultiplexer_1_out_0 ? 1'b1 : 1'bz;  // Driver driver_20
  PullDown pulldown_22 (.out(1'b0));
  PullDown #(.Bits(8)) pulldown_23 (.out({8{1'b0}}));
  assign R = demultiplexer_1_out_5 ? 1'b1 : 1'bz;  // Driver driver_21
  PullDown pulldown_24 (.out(R));
  PullDown pulldown_25 (.out(De));
  assign De = demultiplexer_1_out_2 ? 1'b1 : 1'bz;  // Driver driver_22
  assign WRDY = demultiplexer_1_out_1 ? 1'b1 : 1'bz;  // Driver driver_23
  PullDown pulldown_26 (.out(WRDY));

  assign _0 = 1'b0;
  assign Ca = 1'b0;
  assign IR_op_out = 1'b0;
  assign NA = {8{1'b0}};
  assign out_22 = 1'b0;
  assign RDY = 1'b0;
  assign WR = 1'b0;
  assign Y_in = 1'b0;
  assign Y_out = 1'b0;

  // Notes on the sheet:
  //   FETCH
  //   ADD
endmodule
